// Logisim project disp_example.circ as structural Verilog: 1 circuit, main circuit main
module main (
);

  wire clock_1_out;
  wire [6:0] rom_1_data, rom_2_data;
  wire [13:0] counter_1_q;
  wire [23:0] rom_3_data;

  Clock clock_1 (.out(clock_1_out));
  Counter #(.max('h3fff), .width(14)) counter_1 (
    .Q(counter_1_q), .clk(clock_1_out));  // open: load, D, count, carry, up, clr
  ROM #(.addrWidth(14), .dataWidth(7)) rom_1 (.addr(counter_1_q), .data(rom_1_data));
  ROM #(.addrWidth(14), .dataWidth(7)) rom_2 (.addr(counter_1_q), .data(rom_2_data));
  ROM #(.addrWidth(14), .dataWidth(24)) rom_3 (.addr(counter_1_q), .data(rom_3_data));
  // RGB_Video rgb_video_1: pin names not known; wires that end beside it: clock_1_out, clock_1_out, rom_1_data, rom_2_data, rom_3_data

  // Notes on the sheet:
  //   contents of rom_1 (hex, n*v repeats v):
  //   0 1 2 3 4 5 6 7 8 9 a b c d e f 10 11 12 13 14 15 16 17 18 19 1a 1b 1c 1d 1e 1f 20 21 22 23 24 25 26
  //   27 28 29 2a 2b 2c 2d 2e 2f 30 31 32 33 34 35 36 37 38 39 3a 3b 3c 3d 3e 3f 40 41 42 43 44 45 46 47
  //   48 49 4a 4b 4c 4d 4e 4f 50 51 52 53 54 55 56 57 58 59 5a 5b 5c 5d 5e 5f 60 61 62 63 64 65 66 67 68
  //   69 6a 6b 6c 6d 6e 6f 70 71 72 73 74 75 76 77 78 79 7a 7b 7c 7d 7e 7f 0 1 2 3 4 5 6 7 8 9 a b c d e f
  //   10 11 12 13 14 15 16 17 18 19 1a 1b 1c 1d 1e 1f 20 21 22 23 24 25 26 27 28 29 2a 2b 2c 2d 2e 2f 30
  //   31 32 33 34 35 36 37 38 39 3a 3b 3c 3d 3e 3f 40 41 42 43 44 45 46 47 48 49 4a 4b 4c 4d 4e 4f 50 51
  //   52 53 54 55 56 57 58 59 5a 5b 5c 5d 5e 5f 60 61 62 63 64 65 66 67 68 69 6a 6b 6c 6d 6e 6f 70 71 72
  //   73 74 75 76 77 78 79 7a 7b 7c 7d 7e 7f 0 1 2 3 4 5 6 7 8 9 a b c d e f 10 11 12 13 14 15 16 17 18 19
  //   1a 1b 1c 1d 1e 1f 20 21 22 23 24 25 26 27 28 29 2a 2b 2c 2d 2e 2f 30 31 32 33 34 35 36 37 38 39 3a
  //   3b 3c 3d 3e 3f 40 41 42 43 44 45 46 47 48 49 4a 4b 4c 4d 4e 4f 50 51 52 53 54 55 56 57 58 59 5a 5b
  //   5c 5d 5e 5f 60 61 62 63 64 65 66 67 68 69 6a 6b 6c 6d 6e 6f 70 71 72 73 74 75 76 77 78 79 7a 7b 7c
  //   7d 7e 7f 0 1 2 3 4 5 6 7 8 9 a b c d e f 10 11 12 13 14 15 16 17 18 19 1a 1b 1c 1d 1e 1f 20 21 22 23
  //   24 25 26 27 28 29 2a 2b 2c 2d 2e 2f 30 31 32 33 34 35 36 37 38 39 3a 3b 3c 3d 3e 3f 40 41 42 43 44
  //   45 46 47 48 49 4a 4b 4c 4d 4e 4f 50 51 52 53 54 55 56 57 58 59 5a 5b 5c 5d 5e 5f 60 61 62 63 64 65
  //   66 67 68 69 6a 6b 6c 6d 6e 6f 70 71 72 73 74 75 76 77 78 79 7a 7b 7c 7d 7e 7f 0 1 2 3 4 5 6 7 8 9 a
  //   b c d e f 10 11 12 13 14 15 16 17 18 19 1a 1b 1c 1d 1e 1f 20 21 22 23 24 25 26 27 28 29 2a 2b 2c 2d
  //   2e 2f 30 31 32 33 34 35 36 37 38 39 3a 3b 3c 3d 3e 3f 40 41 42 43 44 45 46 47 48 49 4a 4b 4c 4d 4e
  //   4f 50 51 52 53 54 55 56 57 58 59 5a 5b 5c 5d 5e 5f 60 61 62 63 64 65 66 67 68 69 6a 6b 6c 6d 6e 6f
  //   70 71 72 73 74 75 76 77 78 79 7a 7b 7c 7d 7e 7f 0 1 2 3 4 5 6 7 8 9 a b c d e f 10 11 12 13 14 15 16
  //   17 18 19 1a 1b 1c 1d 1e 1f 20 21 22 23 24 25 26 27 28 29 2a 2b 2c 2d 2e 2f 30 31 32 33 34 35 36 37
  //   38 39 3a 3b 3c 3d 3e 3f 40 41 42 43 44 45 46 47 48 49 4a 4b 4c 4d 4e 4f 50 51 52 53 54 55 56 57 58
  //   59 5a 5b 5c 5d 5e 5f 60 61 62 63 64 65 66 67 68 69 6a 6b 6c 6d 6e 6f 70 71 72 73 74 75 76 77 78 79
  //   7a 7b 7c 7d 7e 7f 0 1 2 3 4 5 6 7 8 9 a b c d e f 10 11 12 13 14 15 16 17 18 19 1a 1b 1c 1d 1e 1f 20
  //   21 22 23 24 25 26 27 28 29 2a 2b 2c 2d 2e 2f 30 31 32 33 34 35 36 37 38 39 3a 3b 3c 3d 3e 3f 40 41
  //   42 43 44 45 46 47 48 49 4a 4b 4c 4d 4e 4f 50 51 52 53 54 55 56 57 58 59 5a 5b 5c 5d 5e 5f 60 61 62
  //   63 64 65 66 67 68 69 6a 6b 6c 6d 6e 6f 70 71 72 73 74 75 76 77 78 79 7a 7b 7c 7d 7e 7f 0 1 2 3 4 5 6
  //   7 8 9 a b c d e f 10 11 12 13 14 15 16 17 18 19 1a 1b 1c 1d 1e 1f 20 21 22 23 24 25 26 27 28 29 2a
  //   2b 2c 2d 2e 2f 30 31 32 33 34 35 36 37 38 39 3a 3b 3c 3d 3e 3f 40 41 42 43 44 45 46 47 48 49 4a 4b
  //   4c 4d 4e 4f 50 51 52 53 54 55 56 57 58 59 5a 5b 5c 5d 5e 5f 60 61 62 63 64 65 66 67 68 69 6a 6b 6c
  //   6d 6e 6f 70 71 72 73 74 75 76 77 78 79 7a 7b 7c 7d 7e 7f 0 1 2 3 4 5 6 7 8 9 a b c d e f 10 11 12 13
  //   14 15 16 17 18 19 1a 1b 1c 1d 1e 1f 20 21 22 23 24 25 26 27 28 29 2a 2b 2c 2d 2e 2f 30 31 32 33 34
  //   35 36 37 38 39 3a 3b 3c 3d 3e 3f 40 41 42 43 44 45 46 47 48 49 4a 4b 4c 4d 4e 4f 50 51 52 53 54 55
  //   56 57 58 59 5a 5b 5c 5d 5e 5f 60 61 62 63 64 65 66 67 68 69 6a 6b 6c 6d 6e 6f 70 71 72 73 74 75 76
  //   77 78 79 7a 7b 7c 7d 7e 7f 0 1 2 3 4 5 6 7 8 9 a b c d e f 10 11 12 13 14 15 16 17 18 19 1a 1b 1c 1d
  //   1e 1f 20 21 22 23 24 25 26 27 28 29 2a 2b 2c 2d 2e 2f 30 31 32 33 34 35 36 37 38 39 3a 3b 3c 3d 3e
  //   3f 40 41 42 43 44 45 46 47 48 49 4a 4b 4c 4d 4e 4f 50 51 52 53 54 55 56 57 58 59 5a 5b 5c 5d 5e 5f
  //   60 61 62 63 64 65 66 67 68 69 6a 6b 6c 6d 6e 6f 70 71 72 73 74 75 76 77 78 79 7a 7b 7c 7d 7e 7f 0 1
  //   2 3 4 5 6 7 8 9 a b c d e f 10 11 12 13 14 15 16 17 18 19 1a 1b 1c 1d 1e 1f 20 21 22 23 24 25 26 27
  //   28 29 2a 2b 2c 2d 2e 2f 30 31 32 33 34 35 36 37 38 39 3a 3b 3c 3d 3e 3f 40 41 42 43 44 45 46 47 48
  //   49 4a 4b 4c 4d 4e 4f 50 51 52 53 54 55 56 57 58 59 5a 5b 5c 5d 5e 5f 60 61 62 63 64 65 66 67 68 69
  //   6a 6b 6c 6d 6e 6f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
  //   contents of rom_2 (hex, n*v repeats v):
  //   128*7f 128*7e 128*7d 128*7c 128*7b 128*7a 128*79 128*78 128*77 128*76 128*75 128*74 128*73 128*72
  //   128*71 128*70 128*6f 128*6e 128*6d 128*6c 128*6b 128*6a 128*69 128*68 128*67 128*66 128*65 128*64
  //   128*63 128*62 128*61 128*60 128*5f 128*5e 128*5d 128*5c 128*5b 128*5a 128*59 128*58 128*57 128*56
  //   128*55 128*54 128*53 128*52 128*51 128*50 128*4f 128*4e 128*4d 128*4c 128*4b 128*4a 128*49 128*48
  //   128*47 128*46 128*45 128*44 128*43 128*42 128*41 128*40 128*3f 128*3e 128*3d 128*3c 128*3b 128*3a
  //   128*39 128*38 128*37 128*36 128*35 128*34 128*33 128*32 128*31 128*30 128*2f 128*2e 128*2d 128*2c
  //   128*2b 128*2a 128*29 128*28 128*27 128*26 128*25 128*24 128*23 128*22 128*21 128*20 128*1f 128*1e
  //   128*1d 128*1c 128*1b 128*1a 128*19 128*18 128*17 128*16 128*15 128*14 128*13 128*12 128*11 128*10
  //   128*f 128*e 128*d 128*c 128*b 128*a 128*9 128*8 128*7 128*6 128*5 128*4 128*3 128*2 128*1
  //   contents of rom_3 (hex, n*v repeats v):
  //   1152*ffffff fefefe ffffff ffffff fefefe fefefe 4*ffffff fefefe ffffff ffffff fefefe fefefe ffffff
  //   ffffff fefefe 7*ffffff fefefe ffffff fefefe ffffff fefefe 4*ffffff fefefe ffffff ffffff fefefe
  //   fefefe ffffff ffffff fefefe ffffff fefefe ffffff ffffff ffffff fefefe 5*ffffff fefefe fefefe
  //   8*ffffff fefefe 6*ffffff fefefe ffffff ffffff fefefe fefefe ffffff ffffff fefefe 9*ffffff fefefe
  //   8*ffffff fefefe fefefe 4*ffffff fefefe 8*ffffff fefefe fefefe 17*ffffff fefefe 6*ffffff fefefe
  //   fefefe ffffff ffffff fefefe fefefe ffffff fefefe 12*ffffff fefefe 7*ffffff fefefe ffffff ffffff
  //   ffffff fefefe ffffff fefefe ffffff ffffff ffffff fefefe ffffff fefefe ffffff ffffff ffffff fefefe
  //   fefefe 15*ffffff fefefe ffffff ffffff ffffff fefefe ffffff ffffff fefefe 9*ffffff fefefe 8*ffffff
  //   fefefe fefefe 4*ffffff fefefe 8*ffffff fefefe fefefe fefefe ffffff fefefe 17*ffffff fefefe fdfdfd
  //   ffffff ffffff fefefe 5*ffffff fefefe 7*ffffff fefefe ffffff ffffff fdfdfd fefefe fefefe ffffff
  //   ffffff fefefe ffffff ffffff 4*fefefe ffffff ffffff fefefe ffffff fefefe ffffff fefefe ffffff fefefe
  //   ffffff fefefe fefefe fefefe ffffff fefefe fefefe ffffff fefefe fefefe 4*ffffff 6*fefefe ffffff
  //   ffffff fefefe ffffff ffffff fefefe fefefe ffffff ffffff fefefe ffffff 6*fefefe ffffff fefefe fefefe
  //   fefefe ffffff fefefe ffffff fefefe fefefe ffffff fefefe fefefe ffffff fefefe fefefe ffffff ffffff
  //   ffffff fefefe ffffff ffffff ffffff fefefe ffffff ffffff fefefe ffffff ffffff fefefe ffffff fefefe
  //   ffffff fefefe fefefe 11*ffffff fefefe fdfdfd fefefe ffffff fefefe ffffff fefefe fefefe ffffff fefefe
  //   fefefe fefefe ffffff ffffff fefefe ffffff fefefe fefefe fefefe ffffff fefefe fefefe ffffff fefefe
  //   fefefe fdfdfd ffffff ffffff fefefe fdfdfd fdfdfd ffffff 4*fefefe 5*ffffff fefefe fefefe ffffff
  //   fefefe fefefe fefefe ffffff ffffff fefefe ffffff 6*fefefe ffffff fefefe 6*ffffff fefefe fefefe
  //   ffffff ffffff ffffff fefefe ffffff fefefe ffffff 4*fefefe ffffff 4*fefefe ffffff 4*fefefe ffffff
  //   ffffff fefefe 5*ffffff fefefe fefefe fdfdfd ffffff ffffff fefefe 4*ffffff fdfdfd 4*ffffff fefefe
  //   ffffff 9*fefefe 6*ffffff fefefe ffffff fefefe fefefe 5*ffffff 4*fefefe ffffff ffffff ffffff fefefe
  //   fefefe fefefe ffffff fefefe ffffff fdfdfd fdfdfd fdfdfd fcfcfc fdfdfd fdfdfd fdfdfd fcfcfc fefefe
  //   ffffff 4*fefefe ffffff fefefe ffffff fefefe ffffff fefefe fefefe fdfdfd ffffff ffffff fefefe fefefe
  //   ffffff fefefe ffffff fdfdfd fefefe fefefe ffffff ffffff fefefe fefefe ffffff fdfdfd ffffff fefefe
  //   6*ffffff fefefe 4*ffffff 4*fefefe 7*ffffff fefefe fefefe 4*fdfdfd fefefe fefefe fcfcfc fcfcfc fefefe
  //   fefefe fefefe ffffff ffffff ffffff fefefe ffffff ffffff ffffff fefefe ffffff ffffff ffffff fefefe
  //   ffffff ffffff ffffff fefefe ffffff ffffff fefefe fefefe ffffff fefefe ffffff ffffff fefefe 7*ffffff
  //   fefefe ffffff fdfdfd 6*ffffff fefefe 8*ffffff fdfdfd fefefe fefefe fdfdfd e5e5e5 a5a5a5 535353
  //   505050 484848 9a9a9a dddddd fefefe fefefe 14*ffffff fefefe 4*ffffff fefefe ffffff fefefe 6*ffffff
  //   fefefe ffffff ffffff fefefe fefefe fefefe ffffff fefefe ffffff ffffff ffffff fdfdfd 11*ffffff fefefe
  //   fefefe fcfcfc e7e7e7 b1b1b1 9a9a9a 484848 4b4b4b 4b4b4b 484848 939393 c6c6c6 e7e7e7 fefefe fdfdfd
  //   ffffff fefefe fefefe 4*ffffff fefefe 6*ffffff fefefe ffffff ffffff ffffff fefefe 13*ffffff fefefe
  //   ffffff ffffff fefefe fefefe fefefe 4*ffffff fefefe fefefe fefefe ffffff fefefe fcfcfc ffffff ffffff
  //   fefefe e8e8e8 404040 50505 20202 10101 0 0 10101 10101 212121 d1d1d1 fefefe ffffff ffffff 4*fefefe
  //   ffffff fefefe ffffff fefefe fdfdfd fefefe ffffff ffffff fefefe fefefe ffffff ffffff fefefe ffffff
  //   4*fefefe ffffff ffffff fefefe ffffff ffffff fefefe 4*ffffff fefefe fefefe fefefe ffffff ffffff
  //   ffffff fefefe fefefe fefefe ffffff ffffff ffffff fefefe fdfdfd fefefe fefefe fafafa c3c3c3 2a2a2a
  //   30303 0 10101 4*0 20202 10101 50505 323232 b9b9b9 f9f9f9 fdfdfd ffffff ffffff fcfcfc ffffff fefefe
  //   ffffff fefefe ffffff fefefe fefefe fefefe ffffff fefefe ffffff fefefe 5*ffffff fefefe ffffff fefefe
  //   6*ffffff fefefe ffffff ffffff fefefe 4*ffffff fefefe fefefe ffffff ffffff fefefe ffffff fe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
endmodule
