// Logisim project tty_example.circ as structural Verilog: 1 circuit, main circuit main
module main (
);

  wire button_1_out, clock_1_out;
  wire [6:0] rom_1_data;
  wire [8:0] counter_1_q;

  Clock clock_1 (.out(clock_1_out));
  ROM #(.addrWidth(9), .dataWidth(7)) rom_1 (.addr(counter_1_q), .data(rom_1_data));
  Counter #(.max('h1ff), .width(9)) counter_1 (
    .Q(counter_1_q), .clk(clock_1_out));  // open: load, D, count, carry, up, clr
  Button button_1 (.out(button_1_out));
  TTY tty_1 (.data(rom_1_data), .clk(clock_1_out), .clr(button_1_out));  // open: we

  // Notes on the sheet:
  //   contents of rom_1 (hex, n*v repeats v):
  //   4c 6f 72 65 6d 20 69 70 73 75 6d 20 64 6f 6c 6f 72 20 73 69 74 20 61 6d 65 74 2c 20 63 6f 6e 73 65
  //   63 74 65 74 75 72 20 61 64 69 70 69 73 63 69 6e 67 20 65 6c 69 74 2e 20 41 6c 69 71 75 61 6d 20 76
  //   65 6c 20 69 61 63 75 6c 69 73 20 6c 69 67 75 6c 61 2c 20 73 65 64 20 64 69 67 6e 69 73 73 69 6d 20
  //   65 72 6f 73 2e 20 4d 61 65 63 65 6e 61 73 20 73 65 6d 70 65 72 2c 20 6e 75 6c 6c 61 20 71 75 69 73
  //   20 70 65 6c 6c 65 6e 74 65 73 71 75 65 20 64 61 70 69 62 75 73 2c 20 6c 69 62 65 72 6f 20 73 65 6d
  //   20 73 6f 6c 6c 69 63 69 74 75 64 69 6e 20 6c 65 6f 2c 20 76 65 6c 20 63 6f 6d 6d 6f 64 6f 20 65 6e
  //   69 6d 20 65 6e 69 6d 20 65 6c 65 6d 65 6e 74 75 6d 20 64 6f 6c 6f 72 2e 20 4d 6f 72 62 69 20 66 65
  //   75 67 69 61 74 20 6d 65 74 75 73 20 76 65 6c 20 6e 75 6c 6c 61 20 73 6f 6c 6c 69 63 69 74 75 64 69
  //   6e 2c 20 76 69 74 61 65 20 63 6f 6e 64 69 6d 65 6e 74 75 6d 20 73 61 70 69 65 6e 20 65 66 66 69 63
  //   69 74 75 72 2e 20 50 68 61 73 65 6c 6c 75 73 20 61 20 6c 61 6f 72 65 65 74 20 73 61 70 69 65 6e 2e
endmodule
