// Logisim project display_control_v2.circ as structural Verilog: 3 circuits, main circuit main
module main (
  input  CLOCK,
  input  DATA1,
  input  DATA2,
  input  DATA3,
  input  DATA4
);

  wire A, B, C, D, D1, D2, D3, D4, display_controller_1_a1, display_controller_1_a2, display_controller_1_a3,
       display_controller_1_a4, display_controller_1_b1, display_controller_1_b2, display_controller_1_b3,
       display_controller_1_b4, display_controller_1_c1, display_controller_1_c2, display_controller_1_c3,
       display_controller_1_c4, display_controller_1_d1, display_controller_1_d2, display_controller_1_d3,
       display_controller_1_d4, display_controller_1_e1, display_controller_1_e2, display_controller_1_e3,
       display_controller_1_e4, display_controller_1_f1, display_controller_1_f2, display_controller_1_f3,
       display_controller_1_f4, display_controller_1_g1, display_controller_1_g2, display_controller_1_g3,
       display_controller_1_g4, display_controller_1_h1, display_controller_1_h2, display_controller_1_h3,
       display_controller_1_h4, E, F, G, H;

  display_controller display_controller_1 (
    .B1(display_controller_1_b1), .C1(display_controller_1_c1), .D1(display_controller_1_d1),
    .E1(display_controller_1_e1), .F1(display_controller_1_f1), .G1(display_controller_1_g1),
    .H1(display_controller_1_h1), .A3(display_controller_1_a3), .B3(display_controller_1_b3),
    .C3(display_controller_1_c3), .D3(display_controller_1_d3), .E3(display_controller_1_e3),
    .F3(display_controller_1_f3), .G3(display_controller_1_g3), .H3(display_controller_1_h3),
    .A1(display_controller_1_a1), .B2(display_controller_1_b2), .C2(display_controller_1_c2),
    .D2(display_controller_1_d2), .E2(display_controller_1_e2), .F2(display_controller_1_f2),
    .G2(display_controller_1_g2), .H2(display_controller_1_h2), .A4(display_controller_1_a4),
    .B4(display_controller_1_b4), .C4(display_controller_1_c4), .D4(display_controller_1_d4),
    .E4(display_controller_1_e4), .F4(display_controller_1_f4), .G4(display_controller_1_g4),
    .H4(display_controller_1_h4), .A2(display_controller_1_a2), .C(C), .D(D), .E(E), .F(F), .G(G), .H(H),
    .DISP1(D1), .DISP2(D2), .DISP3(D3), .DISP4(D4), .A(A), .B(B));
  _7_Segment_Display #(.active("false")) u_7_segment_display_1 (
    .g(display_controller_1_g1), .f(display_controller_1_f1), .a(display_controller_1_a1),
    .b(display_controller_1_b1), .e(display_controller_1_e1), .d(display_controller_1_d1),
    .c(display_controller_1_c1), .dp(display_controller_1_h1));
  _7_Segment_Display #(.active("false")) u_7_segment_display_2 (
    .g(display_controller_1_g2), .f(display_controller_1_f2), .a(display_controller_1_a2),
    .b(display_controller_1_b2), .e(display_controller_1_e2), .d(display_controller_1_d2),
    .c(display_controller_1_c2), .dp(display_controller_1_h2));
  _7_Segment_Display #(.active("false")) u_7_segment_display_3 (
    .g(display_controller_1_g4), .f(display_controller_1_f4), .a(display_controller_1_a4),
    .b(display_controller_1_b4), .e(display_controller_1_e4), .d(display_controller_1_d4),
    .c(display_controller_1_c4), .dp(display_controller_1_h4));
  _7_Segment_Display #(.active("false")) u_7_segment_display_4 (
    .g(display_controller_1_g3), .f(display_controller_1_f3), .a(display_controller_1_a3),
    .b(display_controller_1_b3), .e(display_controller_1_e3), .d(display_controller_1_d3),
    .c(display_controller_1_c3), .dp(display_controller_1_h3));
  sequential_circuit sequential_circuit_1 (
    .CLK(CLOCK), .DATA1(DATA1), .DATA2(DATA2), .DATA3(DATA3), .DATA4(DATA4), .A(A), .B(B), .C(C), .D(D),
    .E(E), .F(F), .G(G), .H(H), .D1(D1), .D2(D2), .D3(D3), .D4(D4));
endmodule

module display_controller (
  input  A,
  input  B,
  input  C,
  input  D,
  input  E,
  input  F,
  input  G,
  input  H,
  input  DISP1,
  input  DISP2,
  input  DISP3,
  input  DISP4,
  output A1,
  output A2,
  output B1,
  output B2,
  output C1,
  output C2,
  output D1,
  output D2,
  output E1,
  output E2,
  output F1,
  output F2,
  output G1,
  output G2,
  output H1,
  output H2,
  output A3,
  output A4,
  output B3,
  output B4,
  output C3,
  output C4,
  output D3,
  output D4,
  output E3,
  output E4,
  output F3,
  output F4,
  output G3,
  output G4,
  output H3,
  output H4
);

  Pull_Resistor #(.pull(1)) pull_resistor_1 (.node({H1, G1, F1, E1, D1, C1, B1, A1}));
  assign {H1, G1, F1, E1, D1, C1, B1, A1} = DISP1 ? {H, G, F, E, D, C, B, A} : 8'bz;  // Controlled_Buffer controlled_buffer_1
  Pull_Resistor #(.pull(1)) pull_resistor_2 (.node({H2, G2, F2, E2, D2, C2, B2, A2}));
  assign {H2, G2, F2, E2, D2, C2, B2, A2} = DISP2 ? {H, G, F, E, D, C, B, A} : 8'bz;  // Controlled_Buffer controlled_buffer_2
  Pull_Resistor #(.pull(1)) pull_resistor_3 (.node({H3, G3, F3, E3, D3, C3, B3, A3}));
  assign {H3, G3, F3, E3, D3, C3, B3, A3} = DISP3 ? {H, G, F, E, D, C, B, A} : 8'bz;  // Controlled_Buffer controlled_buffer_3
  Pull_Resistor #(.pull(1)) pull_resistor_4 (.node({H4, G4, F4, E4, D4, C4, B4, A4}));
  assign {H4, G4, F4, E4, D4, C4, B4, A4} = DISP4 ? {H, G, F, E, D, C, B, A} : 8'bz;  // Controlled_Buffer controlled_buffer_4

  // Other names for the same wires on the sheet: DISP1_t[7:0] = {H1, G1, F1, E1, D1, C1, B1, A1};
  //   DISP2_t[7:0] = {H2, G2, F2, E2, D2, C2, B2, A2}; DISP3_t[7:0] = {H3, G3, F3, E3, D3, C3, B3, A3};
  //   DISP4_t[7:0] = {H4, G4, F4, E4, D4, C4, B4, A4}
endmodule

module sequential_circuit (
  input  CLK,
  input  DATA1,
  input  DATA2,
  input  DATA3,
  input  DATA4,
  output A,
  output B,
  output C,
  output D,
  output E,
  output F,
  output G,
  output H,
  output D1,
  output D2,
  output D3,
  output D4
);

  wire and_1_out, and_2_out, and_3_out, and_4_out, and_5_out, and_6_out, and_7_out, and_8_out, and_9_out,
       and_11_out, and_13_out, and_15_out, CLK_t, clock_1_out, comparator_2_eq, comparator_3_eq,
       comparator_4_eq, comparator_5_eq, comparator_6_eq, comparator_7_eq, comparator_8_eq, EN,
       pull_resistor_1_node, pull_resistor_2_node;
  wire [1:0] counter_2_q;
  wire [2:0] CLK_CNT;
  wire [7:0] D1_t, D2_t, D3_t, D4_t;

  not not_1 (CLK_t, CLK);
  Counter #(.max('h7), .width(3)) counter_1 (
    .load(1'b0), .count(1'b1), .Q(CLK_CNT), .up(1'b1), .clk(CLK), .clr(pull_resistor_1_node));  // open: D, carry
  Pull_Resistor pull_resistor_1 (.node(pull_resistor_1_node));
  Comparator #(.mode("unsigned"), .width(3)) comparator_1 (.a(3'b000), .b(CLK_CNT), .eq(EN));  // open: gt, lt
  and and_1 (and_1_out, EN, CLK_t);
  Comparator #(.mode("unsigned"), .width(3)) comparator_2 (
    .a(3'b001), .b(CLK_CNT), .eq(comparator_2_eq));  // open: gt, lt
  and and_2 (and_2_out, comparator_2_eq, CLK_t);
  Comparator #(.mode("unsigned"), .width(3)) comparator_3 (
    .a(3'b010), .b(CLK_CNT), .eq(comparator_3_eq));  // open: gt, lt
  and and_3 (and_3_out, comparator_3_eq, CLK_t);
  Comparator #(.mode("unsigned"), .width(3)) comparator_4 (
    .a(3'b011), .b(CLK_CNT), .eq(comparator_4_eq));  // open: gt, lt
  and and_4 (and_4_out, comparator_4_eq, CLK_t);
  // Probe on D1_t
  Register #(.trigger("falling"), .width(4)) register_1 (
    .D({DATA4, DATA3, DATA2, DATA1}), .Q(D1_t[3:0]), .clk(and_1_out));  // open: en, clr
  Register #(.trigger("falling"), .width(4)) register_2 (
    .D({DATA4, DATA3, DATA2, DATA1}), .Q(D1_t[7:4]), .clk(and_2_out));  // open: en, clr
  // Probe on D2_t
  Register #(.trigger("falling"), .width(4)) register_3 (
    .D({DATA4, DATA3, DATA2, DATA1}), .Q(D2_t[3:0]), .clk(and_3_out));  // open: en, clr
  Register #(.trigger("falling"), .width(4)) register_4 (
    .D({DATA4, DATA3, DATA2, DATA1}), .Q(D2_t[7:4]), .clk(and_4_out));  // open: en, clr
  Register #(.trigger("falling"), .width(4)) register_5 (
    .D({DATA4, DATA3, DATA2, DATA1}), .Q(D3_t[3:0]), .clk(and_5_out));  // open: en, clr
  Comparator #(.mode("unsigned"), .width(3)) comparator_5 (
    .a(3'b100), .b(CLK_CNT), .eq(comparator_5_eq));  // open: gt, lt
  and and_5 (and_5_out, comparator_5_eq, CLK_t);
  Register #(.trigger("falling"), .width(4)) register_6 (
    .D({DATA4, DATA3, DATA2, DATA1}), .Q(D3_t[7:4]), .clk(and_6_out));  // open: en, clr
  Comparator #(.mode("unsigned"), .width(3)) comparator_6 (
    .a(3'b101), .b(CLK_CNT), .eq(comparator_6_eq));  // open: gt, lt
  and and_6 (and_6_out, comparator_6_eq, CLK_t);
  Register #(.trigger("falling"), .width(4)) register_7 (
    .D({DATA4, DATA3, DATA2, DATA1}), .Q(D4_t[3:0]), .clk(and_7_out));  // open: en, clr
  Comparator #(.mode("unsigned"), .width(3)) comparator_7 (
    .a(3'b110), .b(CLK_CNT), .eq(comparator_7_eq));  // open: gt, lt
  and and_7 (and_7_out, comparator_7_eq, CLK_t);
  Register #(.trigger("falling"), .width(4)) register_8 (
    .D({DATA4, DATA3, DATA2, DATA1}), .Q(D4_t[7:4]), .clk(and_8_out));  // open: en, clr
  Comparator #(.mode("unsigned"), .width(3)) comparator_8 (
    .a(3'b111), .b(CLK_CNT), .eq(comparator_8_eq));  // open: gt, lt
  and and_8 (and_8_out, comparator_8_eq, CLK_t);
  // Probe on D3_t
  // Probe on D4_t
  Counter #(.max('h3), .width(2)) counter_2 (
    .load(1'b0), .count(1'b1), .Q(counter_2_q), .up(1'b1), .clk(clock_1_out), .clr(pull_resistor_2_node));  // open: D, carry
  Clock clock_1 (.out(clock_1_out));
  Pull_Resistor pull_resistor_2 (.node(pull_resistor_2_node));
  Multiplexer #(.select(2), .width(8)) multiplexer_1 (
    .in0(D1_t), .in1(D2_t), .in2(D3_t), .in3(D4_t), .out({H, G, F, E, D, C, B, A}), .sel(counter_2_q));
  and and_9 (and_9_out, ~counter_2_q[0], ~counter_2_q[1]);  // AND_Gate
  and and_10 (D1, and_9_out, EN);
  and and_11 (and_11_out, counter_2_q[0], ~counter_2_q[1]);  // AND_Gate
  and and_12 (D2, and_11_out, EN);
  and and_13 (and_13_out, ~counter_2_q[0], counter_2_q[1]);  // AND_Gate
  and and_14 (D3, and_13_out, EN);
  and and_15 (and_15_out, counter_2_q[0], counter_2_q[1]);
  and and_16 (D4, and_15_out, EN);

  // Other names for the same wires on the sheet: REG1[3:0] = {DATA4, DATA3, DATA2, DATA1};
  //   REG2[3:0] = {DATA4, DATA3, DATA2, DATA1}; REG3[3:0] = {DATA4, DATA3, DATA2, DATA1};
  //   REG4[3:0] = {DATA4, DATA3, DATA2, DATA1}; REG5[3:0] = {DATA4, DATA3, DATA2, DATA1};
  //   REG6[3:0] = {DATA4, DATA3, DATA2, DATA1}; REG7[3:0] = {DATA4, DATA3, DATA2, DATA1};
  //   REG8[3:0] = {DATA4, DATA3, DATA2, DATA1}
endmodule
