// Logisim project display_control_V2.circ as structural Verilog: 4 circuits, main circuit main
module main (
  input  CLOCK,
  input  DATA1,
  input  DATA2,
  input  DATA3,
  input  DATA4
);

  wire A, B, C, D, D1, D2, D3, D4, display_controller_1_a1, display_controller_1_a2, display_controller_1_a3,
       display_controller_1_a4, display_controller_1_b1, display_controller_1_b2, display_controller_1_b3,
       display_controller_1_b4, display_controller_1_c1, display_controller_1_c2, display_controller_1_c3,
       display_controller_1_c4, display_controller_1_d1, display_controller_1_d2, display_controller_1_d3,
       display_controller_1_d4, display_controller_1_e1, display_controller_1_e2, display_controller_1_e3,
       display_controller_1_e4, display_controller_1_f1, display_controller_1_f2, display_controller_1_f3,
       display_controller_1_f4, display_controller_1_g1, display_controller_1_g2, display_controller_1_g3,
       display_controller_1_g4, display_controller_1_h1, display_controller_1_h2, display_controller_1_h3,
       display_controller_1_h4, E, F, G, H;

  display_controller display_controller_1 (
    .B1(display_controller_1_b1), .C1(display_controller_1_c1), .D1(display_controller_1_d1),
    .E1(display_controller_1_e1), .F1(display_controller_1_f1), .G1(display_controller_1_g1),
    .H1(display_controller_1_h1), .A3(display_controller_1_a3), .B3(display_controller_1_b3),
    .C3(display_controller_1_c3), .D3(display_controller_1_d3), .E3(display_controller_1_e3),
    .F3(display_controller_1_f3), .G3(display_controller_1_g3), .H3(display_controller_1_h3),
    .A1(display_controller_1_a1), .B2(display_controller_1_b2), .C2(display_controller_1_c2),
    .D2(display_controller_1_d2), .E2(display_controller_1_e2), .F2(display_controller_1_f2),
    .G2(display_controller_1_g2), .H2(display_controller_1_h2), .A4(display_controller_1_a4),
    .B4(display_controller_1_b4), .C4(display_controller_1_c4), .D4(display_controller_1_d4),
    .E4(display_controller_1_e4), .F4(display_controller_1_f4), .G4(display_controller_1_g4),
    .H4(display_controller_1_h4), .A2(display_controller_1_a2), .C(C), .D(D), .E(E), .F(F), .G(G), .H(H),
    .DISP1(D1), .DISP2(D2), .DISP3(D3), .DISP4(D4), .A(A), .B(B));
  _7_Segment_Display #(.active("false")) u_7_segment_display_1 (
    .g(display_controller_1_g1), .f(display_controller_1_f1), .a(display_controller_1_a1),
    .b(display_controller_1_b1), .e(display_controller_1_e1), .d(display_controller_1_d1),
    .c(display_controller_1_c1), .dp(display_controller_1_h1));
  _7_Segment_Display #(.active("false")) u_7_segment_display_2 (
    .g(display_controller_1_g2), .f(display_controller_1_f2), .a(display_controller_1_a2),
    .b(display_controller_1_b2), .e(display_controller_1_e2), .d(display_controller_1_d2),
    .c(display_controller_1_c2), .dp(display_controller_1_h2));
  _7_Segment_Display #(.active("false")) u_7_segment_display_3 (
    .g(display_controller_1_g4), .f(display_controller_1_f4), .a(display_controller_1_a4),
    .b(display_controller_1_b4), .e(display_controller_1_e4), .d(display_controller_1_d4),
    .c(display_controller_1_c4), .dp(display_controller_1_h4));
  _7_Segment_Display #(.active("false")) u_7_segment_display_4 (
    .g(display_controller_1_g3), .f(display_controller_1_f3), .a(display_controller_1_a3),
    .b(display_controller_1_b3), .e(display_controller_1_e3), .d(display_controller_1_d3),
    .c(display_controller_1_c3), .dp(display_controller_1_h3));
  sequential_circuit_v2 sequential_circuit_v2_1 (
    .CLK(CLOCK), .DATA1(DATA1), .DATA2(DATA2), .DATA3(DATA3), .DATA4(DATA4), .A(A), .B(B), .C(C), .D(D),
    .E(E), .F(F), .G(G), .H(H), .D1(D1), .D2(D2), .D3(D3), .D4(D4));
endmodule

module display_controller (
  input  A,
  input  B,
  input  C,
  input  D,
  input  E,
  input  F,
  input  G,
  input  H,
  input  DISP1,
  input  DISP2,
  input  DISP3,
  input  DISP4,
  output A1,
  output A2,
  output B1,
  output B2,
  output C1,
  output C2,
  output D1,
  output D2,
  output E1,
  output E2,
  output F1,
  output F2,
  output G1,
  output G2,
  output H1,
  output H2,
  output A3,
  output A4,
  output B3,
  output B4,
  output C3,
  output C4,
  output D3,
  output D4,
  output E3,
  output E4,
  output F3,
  output F4,
  output G3,
  output G4,
  output H3,
  output H4
);

  Pull_Resistor #(.pull(1)) pull_resistor_1 (.node({H1, G1, F1, E1, D1, C1, B1, A1}));
  assign {H1, G1, F1, E1, D1, C1, B1, A1} = DISP1 ? {H, G, F, E, D, C, B, A} : 8'bz;  // Controlled_Buffer controlled_buffer_1
  Pull_Resistor #(.pull(1)) pull_resistor_2 (.node({H2, G2, F2, E2, D2, C2, B2, A2}));
  assign {H2, G2, F2, E2, D2, C2, B2, A2} = DISP2 ? {H, G, F, E, D, C, B, A} : 8'bz;  // Controlled_Buffer controlled_buffer_2
  Pull_Resistor #(.pull(1)) pull_resistor_3 (.node({H3, G3, F3, E3, D3, C3, B3, A3}));
  assign {H3, G3, F3, E3, D3, C3, B3, A3} = DISP3 ? {H, G, F, E, D, C, B, A} : 8'bz;  // Controlled_Buffer controlled_buffer_3
  Pull_Resistor #(.pull(1)) pull_resistor_4 (.node({H4, G4, F4, E4, D4, C4, B4, A4}));
  assign {H4, G4, F4, E4, D4, C4, B4, A4} = DISP4 ? {H, G, F, E, D, C, B, A} : 8'bz;  // Controlled_Buffer controlled_buffer_4

  // Other names for the same wires on the sheet: DISP1_t[7:0] = {H1, G1, F1, E1, D1, C1, B1, A1};
  //   DISP2_t[7:0] = {H2, G2, F2, E2, D2, C2, B2, A2}; DISP3_t[7:0] = {H3, G3, F3, E3, D3, C3, B3, A3};
  //   DISP4_t[7:0] = {H4, G4, F4, E4, D4, C4, B4, A4}
endmodule

module sequential_circuit (
  input  CLK,
  input  DATA1,
  input  DATA2,
  input  DATA3,
  input  DATA4,
  output A,
  output B,
  output C,
  output D,
  output E,
  output F,
  output G,
  output H,
  output D1,
  output D2,
  output D3,
  output D4
);

  wire and_1_out, and_2_out, and_3_out, and_4_out, and_5_out, and_6_out, and_7_out, and_8_out, and_9_out,
       CLK_INT_out, not_1_out, not_2_out, not_3_out, not_4_out, not_5_out;
  wire [1:0] counter_2_q;
  wire [2:0] counter_1_q;
  wire [3:0] demultiplexer_1_out0, demultiplexer_1_out1, demultiplexer_1_out2, demultiplexer_1_out3,
       demultiplexer_1_out4, demultiplexer_1_out5, demultiplexer_1_out6, demultiplexer_1_out7, register_1_q,
       register_2_q, register_3_q, register_4_q, register_5_q, register_6_q, register_7_q, register_8_q;

  not not_1 (not_1_out, counter_1_q[2]);
  not not_2 (not_2_out, counter_1_q[1]);
  not not_3 (not_3_out, counter_1_q[0]);
  Counter #(.max('h7), .trigger("falling"), .width(3)) counter_1 (
    .Q(counter_1_q), .clk(CLK));  // open: load, D, count, carry, up, clr
  Clock CLK_INT (.out(CLK_INT_out));
  // Probe on counter_1_q
  Demultiplexer #(.select(3), .width(4)) demultiplexer_1 (
    .out0(demultiplexer_1_out0), .out1(demultiplexer_1_out1), .out2(demultiplexer_1_out2),
    .out3(demultiplexer_1_out3), .out4(demultiplexer_1_out4), .out5(demultiplexer_1_out5),
    .out6(demultiplexer_1_out6), .out7(demultiplexer_1_out7), .in({DATA4, DATA3, DATA2, DATA1}),
    .sel(counter_1_q));
  Counter #(.max('h3), .width(2)) counter_2 (
    .Q(counter_2_q), .clk(CLK_INT_out));  // open: load, D, count, carry, up, clr
  and and_1 (and_1_out, not_1_out, not_2_out, not_3_out, CLK);
  and and_2 (and_2_out, not_1_out, not_2_out, counter_1_q[0], CLK);
  and and_3 (and_3_out, not_1_out, counter_1_q[1], not_3_out, CLK);
  and and_4 (and_4_out, not_1_out, counter_1_q[1], counter_1_q[0], CLK);
  and and_5 (and_5_out, counter_1_q[2], not_2_out, not_3_out, CLK);
  and and_6 (and_6_out, counter_1_q[2], not_2_out, counter_1_q[0], CLK);
  and and_7 (and_7_out, counter_1_q[2], counter_1_q[1], not_3_out, CLK);
  and and_8 (and_8_out, counter_1_q[2], counter_1_q[1], counter_1_q[0], CLK);
  and and_9 (and_9_out, not_1_out, not_2_out, not_3_out);
  and and_10 (D4, counter_2_q[1], counter_2_q[0]);
  and and_11 (D3, counter_2_q[1], not_4_out);
  Register #(.width(4)) register_1 (.D(demultiplexer_1_out0), .Q(register_1_q), .clk(and_1_out));  // open: en, clr
  Register #(.width(4)) register_2 (.D(demultiplexer_1_out1), .Q(register_2_q), .clk(and_2_out));  // open: en, clr
  Register #(.width(4)) register_3 (.D(demultiplexer_1_out2), .Q(register_3_q), .clk(and_3_out));  // open: en, clr
  Register #(.width(4)) register_4 (.D(demultiplexer_1_out3), .Q(register_4_q), .clk(and_4_out));  // open: en, clr
  Register #(.width(4)) register_5 (.D(demultiplexer_1_out4), .Q(register_5_q), .clk(and_5_out));  // open: en, clr
  Register #(.width(4)) register_6 (.D(demultiplexer_1_out5), .Q(register_6_q), .clk(and_6_out));  // open: en, clr
  Register #(.width(4)) register_7 (.D(demultiplexer_1_out6), .Q(register_7_q), .clk(and_7_out));  // open: en, clr
  Register #(.width(4)) register_8 (.D(demultiplexer_1_out7), .Q(register_8_q), .clk(and_8_out));  // open: en, clr
  and and_12 (D2, not_5_out, counter_2_q[0]);
  and and_13 (D1, not_5_out, not_4_out);
  not not_4 (not_4_out, counter_2_q[0]);
  not not_5 (not_5_out, counter_2_q[1]);
  // Probe on {H, G, F, E, D, C, B, A}
  Multiplexer #(.enable("true"), .select(2), .width(8)) multiplexer_1 (
    .in0({register_2_q, register_1_q}), .in1({register_4_q, register_3_q}),
    .in2({register_6_q, register_5_q}), .in3({register_8_q, register_7_q}), .out({H, G, F, E, D, C, B, A}),
    .sel(counter_2_q), .en(and_9_out));
endmodule

module sequential_circuit_v2 (
  input  CLK,
  input  DATA1,
  input  DATA2,
  input  DATA3,
  input  DATA4,
  output A,
  output B,
  output C,
  output D,
  output E,
  output F,
  output G,
  output H,
  output D1,
  output D2,
  output D3,
  output D4
);

  wire CLK_INT_out, n7404_1_pin2, n7404_1_pin4, n7404_1_pin6, n7404_1_pin8, n7404_1_pin10, n7404_1_pin12,
       n7421_1_pin6, n7421_1_pin8, n7421_2_pin6, n7421_2_pin8, n7421_3_pin6, n7421_3_pin8, n7421_4_pin6,
       n7421_4_pin8, n7421_5_pin4, n7421_5_pin10, n7421_6_pin1, n7421_6_pin6, n7421_7_pin4, n7421_7_pin10;
  wire [2:0] n7404_1_pin5, n7404_1_pin11;
  wire [3:0] D0, D1_t, D2_t, D3_t, D4_t, D5, D6, D7, demultiplexer_1_out0, demultiplexer_1_out1,
       demultiplexer_1_out2, demultiplexer_1_out3, demultiplexer_1_out4, demultiplexer_1_out5,
       demultiplexer_1_out6, demultiplexer_1_out7;

  _7404 #(.ShowInternalStructure("true")) u_7404_1 (
    .pin1(n7404_1_pin5[2]), .pin2(n7404_1_pin2), .pin3(n7404_1_pin5[1]), .pin4(n7404_1_pin4),
    .pin5(n7404_1_pin5[0]), .pin6(n7404_1_pin6), .pin13(n7404_1_pin11[1]), .pin12(n7404_1_pin12),
    .pin11(n7404_1_pin11[0]), .pin10(n7404_1_pin10), .pin9(CLK), .pin8(n7404_1_pin8));
  // Probe on {D7, D6, D5, D4_t, D3_t, D2_t, D1_t, D0}
  Clock CLK_INT (.out(CLK_INT_out));
  Counter #(.max('h7), .width(3)) counter_1 (
    .Q(n7404_1_pin11), .clk(CLK_INT_out), .clr(n7404_1_pin11[2]));  // open: load, D, count, carry, up
  Counter #(.max('h7), .width(3)) counter_2 (
    .Q(n7404_1_pin5), .clk(n7404_1_pin8));  // open: load, D, count, carry, up, clr
  Demultiplexer #(.select(3), .width(4)) demultiplexer_1 (
    .out0(demultiplexer_1_out0), .out1(demultiplexer_1_out1), .out2(demultiplexer_1_out2),
    .out3(demultiplexer_1_out3), .out4(demultiplexer_1_out4), .out5(demultiplexer_1_out5),
    .out6(demultiplexer_1_out6), .out7(demultiplexer_1_out7), .in({DATA4, DATA3, DATA2, DATA1}),
    .sel(n7404_1_pin5));
  _7421 #(.ShowInternalStructure("true")) u_7421_1 (
    .pin1(n7404_1_pin2), .pin2(n7404_1_pin4), .pin4(n7404_1_pin6), .pin5(CLK), .pin6(n7421_1_pin6),
    .pin13(n7404_1_pin2), .pin12(n7404_1_pin4), .pin10(n7404_1_pin5[0]), .pin9(CLK), .pin8(n7421_1_pin8));  // open: pin3, pin11
  _7421 #(.ShowInternalStructure("true")) u_7421_2 (
    .pin1(n7404_1_pin2), .pin2(n7404_1_pin5[1]), .pin4(n7404_1_pin6), .pin5(CLK), .pin6(n7421_2_pin6),
    .pin13(n7404_1_pin2), .pin12(n7404_1_pin5[1]), .pin10(n7404_1_pin5[0]), .pin9(CLK), .pin8(n7421_2_pin8));  // open: pin3, pin11
  _7421 #(.ShowInternalStructure("true")) u_7421_3 (
    .pin1(n7404_1_pin5[2]), .pin2(n7404_1_pin4), .pin4(n7404_1_pin6), .pin5(CLK), .pin6(n7421_3_pin6),
    .pin13(n7404_1_pin5[2]), .pin12(n7404_1_pin4), .pin10(n7404_1_pin5[0]), .pin9(CLK), .pin8(n7421_3_pin8));  // open: pin3, pin11
  _7421 #(.ShowInternalStructure("true")) u_7421_4 (
    .pin1(n7404_1_pin5[2]), .pin2(n7404_1_pin5[1]), .pin4(n7404_1_pin6), .pin5(CLK), .pin6(n7421_4_pin6),
    .pin13(n7404_1_pin5[0]), .pin12(n7404_1_pin5[1]), .pin10(n7404_1_pin5[2]), .pin9(CLK), .pin8(n7421_4_pin8));  // open: pin3, pin11
  _74175 #(.ShowInternalStructure("true")) u_74175_1 (
    .pin2(D0[0]), .pin4(demultiplexer_1_out0[0]), .pin5(demultiplexer_1_out0[1]), .pin7(D0[1]),
    .pin15(D0[3]), .pin13(demultiplexer_1_out0[3]), .pin12(demultiplexer_1_out0[2]), .pin10(D0[2]),
    .pin9(n7421_1_pin6));  // open: pin1, pin3, pin6, pin14, pin11
  _74175 #(.ShowInternalStructure("true")) u_74175_2 (
    .pin2(D1_t[0]), .pin4(demultiplexer_1_out1[0]), .pin5(demultiplexer_1_out1[1]), .pin7(D1_t[1]),
    .pin15(D1_t[3]), .pin13(demultiplexer_1_out1[3]), .pin12(demultiplexer_1_out1[2]), .pin10(D1_t[2]),
    .pin9(n7421_1_pin8));  // open: pin1, pin3, pin6, pin14, pin11
  _74175 #(.ShowInternalStructure("true")) u_74175_3 (
    .pin2(D2_t[0]), .pin4(demultiplexer_1_out2[0]), .pin5(demultiplexer_1_out2[1]), .pin7(D2_t[1]),
    .pin15(D2_t[3]), .pin13(demultiplexer_1_out2[3]), .pin12(demultiplexer_1_out2[2]), .pin10(D2_t[2]),
    .pin9(n7421_2_pin6));  // open: pin1, pin3, pin6, pin14, pin11
  _74175 #(.ShowInternalStructure("true")) u_74175_4 (
    .pin2(D3_t[0]), .pin4(demultiplexer_1_out3[0]), .pin5(demultiplexer_1_out3[1]), .pin7(D3_t[1]),
    .pin15(D3_t[3]), .pin13(demultiplexer_1_out3[3]), .pin12(demultiplexer_1_out3[2]), .pin10(D3_t[2]),
    .pin9(n7421_2_pin8));  // open: pin1, pin3, pin6, pin14, pin11
  _74175 #(.ShowInternalStructure("true")) u_74175_5 (
    .pin2(D4_t[0]), .pin4(demultiplexer_1_out4[0]), .pin5(demultiplexer_1_out4[1]), .pin7(D4_t[1]),
    .pin15(D4_t[3]), .pin13(demultiplexer_1_out4[3]), .pin12(demultiplexer_1_out4[2]), .pin10(D4_t[2]),
    .pin9(n7421_3_pin6));  // open: pin1, pin3, pin6, pin14, pin11
  _74175 #(.ShowInternalStructure("true")) u_74175_6 (
    .pin2(D5[0]), .pin4(demultiplexer_1_out5[0]), .pin5(demultiplexer_1_out5[1]), .pin7(D5[1]),
    .pin15(D5[3]), .pin13(demultiplexer_1_out5[3]), .pin12(demultiplexer_1_out5[2]), .pin10(D5[2]),
    .pin9(n7421_3_pin8));  // open: pin1, pin3, pin6, pin14, pin11
  _74175 #(.ShowInternalStructure("true")) u_74175_7 (
    .pin2(D6[0]), .pin4(demultiplexer_1_out6[0]), .pin5(demultiplexer_1_out6[1]), .pin7(D6[1]),
    .pin15(D6[3]), .pin13(demultiplexer_1_out6[3]), .pin12(demultiplexer_1_out6[2]), .pin10(D6[2]),
    .pin9(n7421_4_pin6));  // open: pin1, pin3, pin6, pin14, pin11
  _74175 #(.ShowInternalStructure("true")) u_74175_8 (
    .pin2(D7[0]), .pin4(demultiplexer_1_out7[0]), .pin5(demultiplexer_1_out7[1]), .pin7(D7[1]),
    .pin15(D7[3]), .pin13(demultiplexer_1_out7[3]), .pin12(demultiplexer_1_out7[2]), .pin10(D7[2]),
    .pin9(n7421_4_pin8));  // open: pin1, pin3, pin6, pin14, pin11
  _7421 #(.ShowInternalStructure("true")) u_7421_5 (
    .pin1(n7404_1_pin10), .pin2(n7404_1_pin11[1]), .pin4(n7421_5_pin4), .pin5(n7421_5_pin4), .pin6(D3),
    .pin13(n7404_1_pin12), .pin12(n7404_1_pin10), .pin10(n7421_5_pin10), .pin9(n7421_5_pin10), .pin8(D1));  // open: pin3, pin11
  _7421 #(.ShowInternalStructure("true")) u_7421_6 (
    .pin1(n7421_6_pin1), .pin2(n7404_1_pin2), .pin4(n7404_1_pin4), .pin5(n7404_1_pin6), .pin6(n7421_6_pin6));  // open: pin3, pin13, pin12, pin11, pin10, pin9, pin8
  _7421 #(.ShowInternalStructure("true")) u_7421_7 (
    .pin1(n7404_1_pin11[0]), .pin2(n7404_1_pin11[1]), .pin4(n7421_7_pin4), .pin5(n7421_7_pin4), .pin6(D4),
    .pin13(n7404_1_pin12), .pin12(n7404_1_pin11[0]), .pin10(n7421_7_pin10), .pin9(n7421_7_pin10), .pin8(D2));  // open: pin3, pin11
  Multiplexer #(.disabled("Z"), .enable("true"), .select(2), .width(8)) multiplexer_1 (
    .in0({D1_t, D0}), .in1({D3_t, D2_t}), .in2({D5, D4_t}), .in3({D7, D6}), .out({H, G, F, E, D, C, B, A}),
    .sel(n7404_1_pin11[1:0]), .en(n7421_6_pin6));
  Pull_Resistor #(.pull(1)) pull_resistor_1 (.node({H, G, F, E, D, C, B, A}));
  // Probe on {H, G, F, E, D, C, B, A}
  // also tied to VCC on the sheet: {n7421_5_pin10, n7421_5_pin4, n7421_6_pin1, n7421_7_pin10, n7421_7_pin4}

  // Notes on the sheet:
  //   2x https://www.tme.eu/Document/680025cd9ff53665f3666d199348d4a4/74HC161PW,118.pdf
  //   4x https://www.tme.eu/Document/3f34687dfa88726222cf3a8254a5641d/74HC4051PW-DTE.pd
  //   4x https://www.tme.eu/Document/66247d42a8bbcf67ef2380ef3aaf33d2/74HCT153D.652.pdf
endmodule
