// Logisim project L01_example_BUF_ver02.circ as structural Verilog: 1 circuit, main circuit main
// q
module main (
  input  p,
  output y
);

  Transistor #(.\type ("n")) transistor_1 (.in(1'b1), .out(y), .gate(p));
  Pull_Resistor pull_resistor_1 (.node(y));

  // Notes on the sheet:
  //   Buffer: NMOS + pull-down resistor
endmodule
