// Logisim project L01_example_BUF_ver03.circ as structural Verilog: 1 circuit, main circuit main
// q
module main (
  input  p,
  output y
);

  Pull_Resistor #(.pull(1)) pull_resistor_1 (.node(y));
  Transistor transistor_1 (.in(1'b0), .out(y), .gate(p));

  // Notes on the sheet:
  //   Buffer: PMOS + pull-up resistor
endmodule
