// Logisim project L01_example_NAND_ver01.circ as structural Verilog: 1 circuit, main circuit main
// q
module main (
  input  p,
  input  q,
  output y
);

  wire transistor_2_out;

  Pull_Resistor #(.pull(1)) pull_resistor_1 (.node(y));
  Transistor #(.\type ("n")) transistor_1 (.in(transistor_2_out), .out(y), .gate(p));
  Transistor #(.\type ("n")) transistor_2 (.in(1'b0), .out(transistor_2_out), .gate(q));

  // Notes on the sheet:
  //   NAND gate: NMOS + pull-up resistor
endmodule
