// Logisim project L01_example_NAND_ver02.circ as structural Verilog: 1 circuit, main circuit main
// q
module main (
  input  p,
  input  q,
  output y
);

  wire transistor_4_out;

  Transistor transistor_1 (.in(1'b1), .out(y), .gate(p));
  Transistor transistor_2 (.in(1'b1), .out(y), .gate(q));
  Transistor #(.\type ("n")) transistor_3 (.in(transistor_4_out), .out(y), .gate(p));
  Transistor #(.\type ("n")) transistor_4 (.in(1'b0), .out(transistor_4_out), .gate(q));

  // Notes on the sheet:
  //   NAND gate: 2x NMOS + 2x PMOS (CMOS)
endmodule
