// Logisim project L01_example_NOR_ver01.circ as structural Verilog: 1 circuit, main circuit main
// q
module main (
  input  p,
  input  q,
  output y
);

  wire transistor_1_out;

  Transistor transistor_1 (.in(1'b1), .out(transistor_1_out), .gate(p));
  Pull_Resistor pull_resistor_1 (.node(y));
  Transistor transistor_2 (.in(transistor_1_out), .out(y), .gate(q));

  // Notes on the sheet:
  //   NOR gate: PMOS + pull-down resistor
endmodule
