// Logisim project L01_example_NOR_ver02.circ as structural Verilog: 1 circuit, main circuit main
// q
module main (
  input  p,
  input  q,
  output y
);

  wire transistor_2_out;

  Transistor #(.\type ("n")) transistor_1 (.in(1'b0), .out(y), .gate(q));
  Transistor transistor_2 (.in(1'b1), .out(transistor_2_out), .gate(p));
  Transistor transistor_3 (.in(transistor_2_out), .out(y), .gate(q));
  Transistor #(.\type ("n")) transistor_4 (.in(1'b0), .out(y), .gate(p));

  // Notes on the sheet:
  //   NOR gate: 2x NMOS + 2x PMOS (CMOS)
endmodule
