// Logisim project L01_example_NOT_ver02.circ as structural Verilog: 1 circuit, main circuit main
// q
module main (
  input  p,
  output y
);

  Pull_Resistor #(.pull(1)) pull_resistor_1 (.node(y));
  Transistor #(.\type ("n")) transistor_1 (.in(1'b0), .out(y), .gate(p));

  // Notes on the sheet:
  //   NOT gate: NMOS + pull-up resistor
endmodule
