// Logisim project L01_example_NOT_ver03.circ as structural Verilog: 1 circuit, main circuit main
// q
module main (
  input  p,
  output y
);

  Transistor transistor_1 (.in(1'b1), .out(y), .gate(p));
  Pull_Resistor pull_resistor_1 (.node(y));

  // Notes on the sheet:
  //   NOT gate: PMOS + pull-down resistor
endmodule
