// Logisim project L01_example_OR_ver01.circ as structural Verilog: 1 circuit, main circuit main
module main (
  input  q,
  input  p,
  output y
);

  wire transistor_2_out;

  Pull_Resistor #(.pull(1)) pull_resistor_1 (.node(y));
  Transistor transistor_1 (.in(transistor_2_out), .out(y), .gate(q));
  Transistor transistor_2 (.in(1'b0), .out(transistor_2_out), .gate(p));

  // Notes on the sheet:
  //   OR gate: PMOS + pull-up resistor
endmodule
