// Logisim project L01_example_XOR_ver01.circ as structural Verilog: 1 circuit, main circuit main
module main (
  input  p,
  input  q,
  output y
);

  wire transistor_1_out, transistor_2_out, transistor_3_out, transistor_4_out;

  Transistor transistor_1 (.in(1'b1), .out(transistor_1_out), .gate(q));
  Transistor #(.\type ("n")) transistor_2 (.in(transistor_1_out), .out(transistor_2_out), .gate(p));
  Transistor transistor_3 (.in(1'b1), .out(transistor_3_out), .gate(p));
  Transistor #(.\type ("n")) transistor_4 (.in(transistor_3_out), .out(transistor_4_out), .gate(q));
  Pull_Resistor pull_resistor_1 (.node(transistor_2_out));
  Transistor #(.\type ("n")) transistor_5 (.in(1'b1), .out(y), .gate(transistor_2_out));
  Pull_Resistor pull_resistor_2 (.node(transistor_4_out));
  Transistor #(.\type ("n")) transistor_6 (.in(1'b1), .out(y), .gate(transistor_4_out));
  Pull_Resistor pull_resistor_3 (.node(y));

  // Notes on the sheet:
  //   XOR: 4x NMOS + 2x PMOS
endmodule
