// Logisim project L01_example_XOR_ver02.circ as structural Verilog: 1 circuit, main circuit main
module main (
  input  p,
  input  q,
  output p_xor_q
);

  wire transistor_5_out;

  Transistor transistor_1 (.in(p), .out(p_xor_q), .gate(q));
  Transistor transistor_2 (.in(q), .out(p_xor_q), .gate(p));
  Transistor #(.\type ("n")) transistor_3 (.in(transistor_5_out), .out(p_xor_q), .gate(q));
  Transistor #(.\type ("n")) transistor_4 (.in(q), .out(p_xor_q), .gate(transistor_5_out));
  Transistor transistor_5 (.in(1'b1), .out(transistor_5_out), .gate(p));
  Transistor #(.\type ("n")) transistor_6 (.in(1'b0), .out(transistor_5_out), .gate(p));

  // Notes on the sheet:
  //   XOR: 3x NMOS + 3x PMOS (CMOS)
endmodule
