// Logisim project L01_template_GATE_2IN_1OUT.circ as structural Verilog: 1 circuit, main circuit main
module main (
  input  p,
  input  q,
  output out_3
);

  wire not_p, not_q, transistor_5_out, transistor_6_out, transistor_8_out, transistor_9_out,
       transistor_10_out, transistor_12_out, transistor_13_out, transistor_14_out, transistor_16_out,
       transistor_17_out, transistor_18_out, transistor_20_out;

  Transistor transistor_1 (.in(1'b1), .out(not_p), .gate(p));
  Transistor #(.\type ("n")) transistor_2 (.in(1'b0), .out(not_p), .gate(p));
  Transistor transistor_3 (.in(1'b1), .out(not_q), .gate(q));
  Transistor #(.\type ("n")) transistor_4 (.in(1'b0), .out(not_q), .gate(q));
  Transistor transistor_5 (.in(1'b1), .out(transistor_5_out), .gate(not_p));
  Transistor transistor_6 (.in(transistor_5_out), .out(transistor_6_out), .gate(not_q));
  Transistor #(.\type ("n")) transistor_7 (.in(transistor_8_out), .gate(not_p));  // open: out
  Transistor #(.\type ("n")) transistor_8 (.in(1'b0), .out(transistor_8_out), .gate(not_q));
  Transistor transistor_9 (.in(1'b1), .out(transistor_9_out), .gate(not_p));
  Transistor transistor_10 (.in(transistor_9_out), .out(transistor_10_out), .gate(q));
  Transistor #(.\type ("n")) transistor_11 (.in(transistor_12_out), .gate(not_p));  // open: out
  Transistor #(.\type ("n")) transistor_12 (.in(1'b0), .out(transistor_12_out), .gate(q));
  Transistor transistor_13 (.in(1'b1), .out(transistor_13_out), .gate(p));
  Transistor transistor_14 (.in(transistor_13_out), .out(transistor_14_out), .gate(not_q));
  Transistor #(.\type ("n")) transistor_15 (.in(transistor_16_out), .gate(p));  // open: out
  Transistor #(.\type ("n")) transistor_16 (.in(1'b0), .out(transistor_16_out), .gate(not_q));
  Transistor transistor_17 (.in(1'b1), .out(transistor_17_out), .gate(p));
  Transistor transistor_18 (.in(transistor_17_out), .out(transistor_18_out), .gate(q));
  Transistor #(.\type ("n")) transistor_19 (.in(transistor_20_out), .gate(p));  // open: out
  Transistor #(.\type ("n")) transistor_20 (.in(1'b0), .out(transistor_20_out), .gate(q));
endmodule
