// Logisim project L02_example_LED_line.circ as structural Verilog: 2 circuits, main circuit main
module LED_line_validator (
  input  a,
  input  b,
  input  c,
  input  d,
  input  e,
  output [4:0] out_6,
  output x
);

  wire not_1_out, not_2_out, not_3_out, not_4_out, not_5_out;

  and and_1 (out_6[4], a, x);
  and and_2 (out_6[3], b, x);
  and and_3 (out_6[2], c, x);
  and and_4 (out_6[1], d, x);
  and and_5 (out_6[0], e, x);
  not not_1 (not_1_out, a);
  not not_2 (not_2_out, b);
  not not_3 (not_3_out, c);
  not not_4 (not_4_out, d);
  not not_5 (not_5_out, e);

  // Notes on the sheet:
  //   TODO: Implement logic
endmodule

module main (
  input  a,
  input  b,
  input  c,
  input  d,
  input  e,
  output [4:0] LED_PINS,
  output X
);

  LedBar #(.matrixcols(5)) ledbar_1 (
    .led0(LED_PINS[0]), .led1(LED_PINS[1]), .led2(LED_PINS[2]), .led3(LED_PINS[3]), .led4(LED_PINS[4]));
  LED_line_validator led_line_validator_1 (.a(a), .b(b), .c(c), .d(d), .e(e), .out_6(LED_PINS), .x(X));
  LED led_1 (.in(X));
endmodule
