// Logisim project nor_task_1.circ as structural Verilog: 1 circuit, main circuit main
module main (
  input  a,
  input  b,
  input  c,
  input  d,
  input  e,
  output y
);

  wire nor_1_out, nor_2_out, nor_3_out, nor_4_out, nor_5_out, nor_6_p7, nor_7_p8, nor_8_p8, nor_9_p8,
       nor_10_p8, nor_11_p8, nor_12_p8, nor_13_p8, nor_14_p8, nor_15_p8, nor_16_p8, nor_17_p8, nor_18_p8,
       nor_19_p8, nor_20_p8, nor_21_p8, nor_22_p8, nor_23_p8, nor_24_p8, nor_25_p8, nor_26_p7, undriven,
       undriven_2, undriven_3, undriven_4;

  not nor_1 (nor_1_out, undriven);  // NOR_Gate
  nor nor_2 (nor_2_out, undriven, undriven_2);
  nor nor_3 (nor_3_out, undriven_2, undriven_3);
  nor nor_4 (nor_4_out, undriven_3, undriven_4);
  not nor_5 (nor_5_out, undriven_4);  // NOR_Gate
  // NOR_Gate nor_6: pin names not known; wires that end beside it: a, b, c, d, nor_5_out, a, nor_6_p7
  // NOR_Gate nor_7: pin names not known; wires that end beside it: nor_5_out, a, b, c, nor_4_out, e, a, nor_7_p8
  // NOR_Gate nor_8: pin names not known; wires that end beside it: e, a, b, nor_3_out, d, e, a, nor_8_p8
  // NOR_Gate nor_9: pin names not known; wires that end beside it: e, a, b, nor_3_out, d, nor_5_out, a, nor_9_p8
  // NOR_Gate nor_10: pin names not known; wires that end beside it: nor_5_out, a, b, nor_3_out, nor_4_out, nor_5_out, a, nor_10_p8
  // NOR_Gate nor_11: pin names not known; wires that end beside it: nor_5_out, a, nor_2_out, c, d, e, a, nor_11_p8
  // NOR_Gate nor_12: pin names not known; wires that end beside it: e, a, nor_2_out, c, nor_4_out, e, a, nor_12_p8
  // NOR_Gate nor_13: pin names not known; wires that end beside it: e, a, nor_2_out, c, nor_4_out, nor_5_out, a, nor_13_p8
  // NOR_Gate nor_14: pin names not known; wires that end beside it: nor_5_out, a, nor_2_out, nor_3_out, d, nor_5_out, a, nor_14_p8
  // NOR_Gate nor_15: pin names not known; wires that end beside it: nor_5_out, a, nor_2_out, nor_3_out, nor_4_out, e, nor_1_out, nor_15_p8
  // NOR_Gate nor_16: pin names not known; wires that end beside it: e, nor_1_out, b, c, d, e, nor_1_out, nor_16_p8
  // NOR_Gate nor_17: pin names not known; wires that end beside it: e, nor_1_out, b, c, d, nor_5_out, nor_1_out, nor_17_p8
  // NOR_Gate nor_18: pin names not known; wires that end beside it: nor_5_out, nor_1_out, b, c, nor_4_out, nor_5_out, nor_1_out, nor_18_p8
  // NOR_Gate nor_19: pin names not known; wires that end beside it: nor_5_out, nor_1_out, b, nor_3_out, d, e, nor_1_out, nor_19_p8
  // NOR_Gate nor_20: pin names not known; wires that end beside it: e, nor_1_out, b, nor_3_out, nor_4_out, e, nor_1_out, nor_20_p8
  // NOR_Gate nor_21: pin names not known; wires that end beside it: e, nor_1_out, b, nor_3_out, nor_4_out, nor_5_out, nor_1_out, nor_21_p8
  // NOR_Gate nor_22: pin names not known; wires that end beside it: nor_5_out, nor_1_out, nor_2_out, c, d, nor_5_out, nor_1_out, nor_22_p8
  // NOR_Gate nor_23: pin names not known; wires that end beside it: nor_5_out, nor_1_out, nor_2_out, c, nor_4_out, e, nor_1_out, nor_23_p8
  // NOR_Gate nor_24: pin names not known; wires that end beside it: e, nor_1_out, nor_2_out, nor_3_out, d, e, nor_1_out, nor_24_p8
  // NOR_Gate nor_25: pin names not known; wires that end beside it: e, nor_1_out, nor_2_out, nor_3_out, d, nor_5_out, nor_1_out, nor_25_p8
  // NOR_Gate nor_26: pin names not known; wires that end beside it: nor_5_out, nor_1_out, nor_2_out, nor_3_out, nor_4_out, nor_5_out, nor_26_p7
  // NOR_Gate nor_27: pin names not known; wires that end beside it: nor_6_p7, nor_7_p8, nor_8_p8, nor_9_p8, nor_10_p8, nor_11_p8, nor_12_p8, nor_13_p8, nor_14_p8, nor_15_p8, nor_16_p8, nor_17_p8, nor_18_p8, nor_19_p8, nor_20_p8, nor_21_p8, nor_22_p8, nor_23_p8, nor_24_p8, nor_25_p8, nor_26_p7, y
endmodule
