// Logisim project nor_task_1_rewired.circ as structural Verilog: 1 circuit, main circuit main
module main (
  input  a,
  input  b,
  input  c,
  input  d,
  input  e,
  output y
);

  wire nor_1_out, nor_2_out, nor_3_out, nor_4_out, nor_5_out, nor_6_out, nor_7_out, nor_8_out, nor_9_out,
       nor_10_out, nor_11_out, nor_12_out, nor_13_out, nor_14_out, nor_15_out, nor_16_out, nor_17_out,
       nor_18_out, nor_19_out, nor_20_out, nor_21_out, nor_22_out, nor_23_out, nor_24_out, nor_25_out,
       nor_26_out;

  nor nor_1 (nor_1_out, a, a);
  nor nor_2 (nor_2_out, b, b);
  nor nor_3 (nor_3_out, c, c);
  nor nor_4 (nor_4_out, d, d);
  nor nor_5 (nor_5_out, e, e);
  nor nor_6 (nor_6_out, a, b, c, d, nor_5_out);
  nor nor_7 (nor_7_out, a, b, c, nor_4_out, e);
  nor nor_8 (nor_8_out, a, b, nor_3_out, d, e);
  nor nor_9 (nor_9_out, a, b, nor_3_out, d, nor_5_out);
  nor nor_10 (nor_10_out, a, b, nor_3_out, nor_4_out, nor_5_out);
  nor nor_11 (nor_11_out, a, nor_2_out, c, d, e);
  nor nor_12 (nor_12_out, a, nor_2_out, c, nor_4_out, e);
  nor nor_13 (nor_13_out, a, nor_2_out, c, nor_4_out, nor_5_out);
  nor nor_14 (nor_14_out, a, nor_2_out, nor_3_out, d, nor_5_out);
  nor nor_15 (nor_15_out, a, nor_2_out, nor_3_out, nor_4_out, e);
  nor nor_16 (nor_16_out, nor_1_out, b, c, d, e);
  nor nor_17 (nor_17_out, nor_1_out, b, c, d, nor_5_out);
  nor nor_18 (nor_18_out, nor_1_out, b, c, nor_4_out, nor_5_out);
  nor nor_19 (nor_19_out, nor_1_out, b, nor_3_out, d, e);
  nor nor_20 (nor_20_out, nor_1_out, b, nor_3_out, nor_4_out, e);
  nor nor_21 (nor_21_out, nor_1_out, b, nor_3_out, nor_4_out, nor_5_out);
  nor nor_22 (nor_22_out, nor_1_out, nor_2_out, c, d, nor_5_out);
  nor nor_23 (nor_23_out, nor_1_out, nor_2_out, c, nor_4_out, e);
  nor nor_24 (nor_24_out, nor_1_out, nor_2_out, nor_3_out, d, e);
  nor nor_25 (nor_25_out, nor_1_out, nor_2_out, nor_3_out, d, nor_5_out);
  nor nor_26 (nor_26_out, nor_1_out, nor_2_out, nor_3_out, nor_4_out, nor_5_out);
  nor nor_27 (y, nor_6_out, nor_7_out, nor_8_out, nor_9_out, nor_10_out, nor_11_out, nor_12_out, nor_13_out, nor_14_out, nor_15_out, nor_16_out, nor_17_out, nor_18_out, nor_19_out, nor_20_out, nor_21_out, nor_22_out, nor_23_out, nor_24_out, nor_25_out, nor_26_out);
endmodule
