// Logisim project L05_example_Func02.circ as structural Verilog: 5 circuits, main circuit main
module main (
  input  a,
  input  b,
  input  c,
  input  d,
  input  e,
  output x_gates,
  output x_mux,
  output x_demux,
  output x_rom
);

  FUNC02_Gates func02_gates_1 (.a(a), .b(b), .c(c), .d(d), .e(e), .x(x_gates));
  FUNC02_Mux func02_mux_1 (.a(a), .b(b), .c(c), .d(d), .e(e), .x(x_mux));
  FUNC02_Demux func02_demux_1 (.a(a), .b(b), .c(c), .d(d), .e(e), .x(x_demux));
  FUNC02_Rom func02_rom_1 (.a(a), .b(b), .c(c), .d(d), .e(e), .x(x_rom));

  // Notes on the sheet:
  //   Boolean function #02: LED line control validation
endmodule

module FUNC02_Gates (
  input  a,
  input  b,
  input  c,
  input  d,
  input  e,
  output x
);

  wire and_1_out, and_2_out, and_3_out, not_1_out, not_2_out, not_3_out, not_4_out;

  not not_1 (not_1_out, a);
  not not_2 (not_2_out, b);
  not not_3 (not_3_out, c);
  not not_4 (not_4_out, d);
  and and_1 (and_1_out, not_1_out, not_2_out, not_3_out, not_4_out);
  and and_2 (and_2_out, not_1_out, not_2_out, d, e);
  and and_3 (and_3_out, b, c, d, e);
  or or_1 (x, and_1_out, and_2_out, and_3_out);
endmodule

module FUNC02_Mux (
  input  a,
  input  b,
  input  c,
  input  d,
  input  e,
  output x
);

  Pull_Resistor pull_resistor_1 (.node(x));
endmodule

module FUNC02_Demux (
  input  a,
  input  b,
  input  c,
  input  d,
  input  e,
  output x
);

  Pull_Resistor pull_resistor_1 (.node(x));
endmodule

module FUNC02_Rom (
  input  a,
  input  b,
  input  c,
  input  d,
  input  e,
  output x
);

  Pull_Resistor pull_resistor_1 (.node(x));
endmodule
