// Logisim project L05_example_Func03.circ as structural Verilog: 5 circuits, main circuit main
module main (
  input  [1:0] n1,
  input  [1:0] n2,
  output x_gates,
  output x_mux,
  output x_demux,
  output x_rom
);

  FUNC03_Gates func03_gates_1 (.a(n1[1]), .b(n1[0]), .c(n2[1]), .d(n2[0]), .x(x_gates));
  FUNC03_Mux func03_mux_1 (.a(n1[1]), .b(n1[0]), .c(n2[1]), .d(n2[0]), .x(x_mux));
  FUNC03_Demux func03_demux_1 (.a(n1[1]), .b(n1[0]), .c(n2[1]), .d(n2[0]), .x(x_demux));
  FUNC03_Rom func03_rom_1 (.a(n1[1]), .b(n1[0]), .c(n2[1]), .d(n2[0]), .x(x_rom));

  // Notes on the sheet:
  //   Boolean function #03: two bit integer comparator 
  //   (n1 <= n2)
endmodule

module FUNC03_Gates (
  input  a,
  input  b,
  input  c,
  input  d,
  output x
);

  wire and_1_out, and_2_out, and_3_out, and_4_out, and_5_out, not_1_out, not_2_out;

  not not_1 (not_1_out, a);
  not not_2 (not_2_out, b);
  and and_1 (and_1_out, not_1_out, not_2_out);
  and and_2 (and_2_out, not_1_out, d);
  and and_3 (and_3_out, not_1_out, c);
  and and_4 (and_4_out, not_2_out, c);
  and and_5 (and_5_out, c, d);
  or or_1 (x, and_1_out, and_2_out, and_3_out, and_4_out, and_5_out);
endmodule

module FUNC03_Mux (
  input  a,
  input  b,
  input  c,
  input  d,
  output x
);

  Pull_Resistor pull_resistor_1 (.node(x));
endmodule

module FUNC03_Demux (
  input  a,
  input  b,
  input  c,
  input  d,
  output x
);

  Pull_Resistor pull_resistor_1 (.node(x));
endmodule

module FUNC03_Rom (
  input  a,
  input  b,
  input  c,
  input  d,
  output x
);

  Pull_Resistor pull_resistor_1 (.node(x));
endmodule
