// Logisim project d_latch_example.circ as structural Verilog: 1 circuit, main circuit main
module main (
  input  in_1,
  output Q,
  output nQ,
  output Eq
);

  wire and_3_out, and_4_out, EN, R, S;

  Clock clock_1 (.out(EN));
  and and_1 (R, ~in_1, EN);  // AND_Gate
  and and_2 (S, EN, in_1);
  and and_3 (and_3_out, in_1, EN);
  or or_1 (Eq, and_3_out, and_4_out);
  and and_4 (and_4_out, ~EN, Q);  // AND_Gate
  nor nor_1 (Q, nQ, R);
  nor nor_2 (nQ, Q, S);

  // Other names for the same wires on the sheet: D = in_1

  // Notes on the sheet:
  //   D Latch implementation with NOR gates
endmodule
