// Logisim project demux_example.circ as structural Verilog: 1 circuit, main circuit main
module main (
  input  A,
  input  B,
  input  C,
  input  D,
  output f
);

  wire demultiplexer_1_out0, demultiplexer_1_out3, demultiplexer_1_out7, demultiplexer_1_out9,
       demultiplexer_1_out10, demultiplexer_1_out13, demultiplexer_1_out14, demultiplexer_1_out15,
       pull_resistor_1_node, pull_resistor_2_node;

  Pull_Resistor #(.pull(1)) pull_resistor_1 (.node(pull_resistor_1_node));
  Demultiplexer #(.select(4)) demultiplexer_1 (
    .out0(demultiplexer_1_out0), .out3(demultiplexer_1_out3), .out7(demultiplexer_1_out7),
    .out9(demultiplexer_1_out9), .out10(demultiplexer_1_out10), .out13(demultiplexer_1_out13),
    .out14(demultiplexer_1_out14), .out15(demultiplexer_1_out15), .in(pull_resistor_1_node),
    .sel({A, B, C, D}), .en(pull_resistor_2_node));  // open: out1, out2, out4, out5, out6, out8, out11, out12
  Pull_Resistor #(.pull(1)) pull_resistor_2 (.node(pull_resistor_2_node));
  or or_1 (f, demultiplexer_1_out0, demultiplexer_1_out3, demultiplexer_1_out7, demultiplexer_1_out9, demultiplexer_1_out10, demultiplexer_1_out13, demultiplexer_1_out14, demultiplexer_1_out15);
endmodule
