// Logisim project jk_latch_example.circ as structural Verilog: 1 circuit, main circuit main
module main (
  input  K,
  input  J,
  output Q,
  output nQ
);

  wire and_1_out, and_2_out, button_1_out;

  Button button_1 (.out(button_1_out));
  and and_1 (and_1_out, Q, K, button_1_out);
  and and_2 (and_2_out, button_1_out, J, nQ);
  nor nor_1 (Q, and_1_out, nQ);
  nor nor_2 (nQ, Q, and_2_out);

  // Notes on the sheet:
  //   Q: pull=down
  //   nQ: pull=down
endmodule
