// Logisim project mux_example.circ as structural Verilog: 1 circuit, main circuit main
module main (
  input  A,
  input  B,
  input  C,
  input  D,
  output f
);

  wire pull_resistor_1_node, pull_resistor_2_node, pull_resistor_3_node;

  Pull_Resistor pull_resistor_1 (.node(pull_resistor_1_node));
  Pull_Resistor #(.pull(1)) pull_resistor_2 (.node(pull_resistor_2_node));
  Multiplexer #(.enable("true"), .select(4)) multiplexer_1 (
    .in0(pull_resistor_2_node), .in1(pull_resistor_1_node), .in2(pull_resistor_1_node),
    .in3(pull_resistor_2_node), .in4(pull_resistor_1_node), .in5(pull_resistor_1_node),
    .in6(pull_resistor_1_node), .in7(pull_resistor_2_node), .in8(pull_resistor_1_node),
    .in9(pull_resistor_2_node), .in10(pull_resistor_2_node), .in11(pull_resistor_1_node),
    .in12(pull_resistor_1_node), .in13(pull_resistor_2_node), .in14(pull_resistor_2_node),
    .in15(pull_resistor_2_node), .out(f), .sel({A, B, C, D}), .en(pull_resistor_3_node));
  Pull_Resistor #(.pull(1)) pull_resistor_3 (.node(pull_resistor_3_node));
endmodule
