// Logisim project rom_example.circ as structural Verilog: 1 circuit, main circuit main
module main (
  input  A,
  input  B,
  input  C,
  input  D,
  output f
);

  ROM #(.addrWidth(4), .dataWidth(1)) rom_1 (.addr({A, B, C, D}));  // open: data

  // Notes on the sheet:
  //   contents of rom_1 (hex, n*v repeats v):
  //   1 0 0 1 0 0 0 1 0 1 1 0 0 1 1 1
endmodule
