// Logisim project rs_latch_example.circ as structural Verilog: 1 circuit, main circuit main
module main (
  input  R,
  input  S,
  output Q,
  output nQ,
  output Eq
);

  wire and_1_out;

  nor nor_1 (Q, nQ, R);
  Pull_Resistor pull_resistor_1 (.node(nQ));
  nor nor_2 (nQ, Q, S);
  or or_1 (Eq, S, and_1_out);
  and and_1 (and_1_out, ~R, Q);  // AND_Gate
  Pull_Resistor #(.pull(1)) pull_resistor_2 (.node(Q));

  // Notes on the sheet:
  //   RS Latch implementation with NOR gates
  //   nor_1 drives only 0 and floats otherwise
  //   nor_2 drives only 1 and floats otherwise
  //   RS Latch characterisitc equation
endmodule
