// Logisim project moore_machine.circ as structural Verilog: 1 circuit, main circuit main
module main (
  input  [1:0] INPUT,
  output [2:0] OUTPUT
);

  wire and_1_out, and_2_out, and_3_out, and_4_out, ENABLE_out;
  wire [1:0] rom_1_data;
  wire [3:2] register_1_q;

  Button ENABLE (.out(ENABLE_out));
  LED a (.in(and_1_out));
  LED b (.in(and_2_out));
  and and_1 (and_1_out, ~INPUT[0], ~INPUT[1]);  // AND_Gate
  and and_2 (and_2_out, INPUT[0], ~INPUT[1]);  // AND_Gate
  LED c (.in(and_3_out));
  LED d (.in(and_4_out));
  and and_3 (and_3_out, ~INPUT[0], INPUT[1]);  // AND_Gate
  and and_4 (and_4_out, INPUT[1], INPUT[0]);
  ROM #(.addrWidth(4), .dataWidth(2)) rom_1 (.addr({register_1_q, INPUT}), .data(rom_1_data));
  Register #(.width(2)) register_1 (.D(rom_1_data), .clk(ENABLE_out), .Q(register_1_q));  // open: en, clr
  ROM #(.addrWidth(2), .dataWidth(3)) rom_2 (.addr(register_1_q), .data(OUTPUT));
  LED sA (.in(OUTPUT[0]));
  LED sB (.in(OUTPUT[1]));
  LED sC (.in(OUTPUT[2]));

  // Notes on the sheet:
  //   INPUT VISUALISATION
  //   contents of rom_1 (hex, n*v repeats v):
  //   0 1 2 0 1 0 2 0 2 1 0 0 4*3
  //   NEXT STATE LOGIC
  //   STATE 
  //   REGISTER
  //   contents of rom_2 (hex, n*v repeats v):
  //   1 2 4
  //   STATE/OUTPUT VISUALISATION
  //   OUTPUT LOGIC
endmodule
