// Logisim project moore_machine_v2.circ as structural Verilog: 7 circuits, main circuit main
module main (
  output [1:0] INPUT,
  output [2:0] OUTPUT
);

  wire clock_1_out, Inputs_a, Inputs_b, Inputs_c, Inputs_d, Outputs_alpha, Outputs_beta, Outputs_gamma,
       States_a, States_b, States_c, undriven, undriven_2;
  wire [1:0] nextstatelogic_1_ns, register_1_q;

  Clock clock_1 (.out(clock_1_out));
  LED a (.in(Inputs_a));
  TestSequence testsequence_1 (.CLK(clock_1_out), .I_test(INPUT));
  LED b (.in(Inputs_b));
  LED c (.in(Inputs_c));
  LED d (.in(Inputs_d));
  InputVisualisation Inputs (.I(INPUT), .a(Inputs_a), .b(Inputs_b), .c(Inputs_c), .d(Inputs_d));
  NextStateLogic nextstatelogic_1 (.I(INPUT), .S(register_1_q), .NS(nextstatelogic_1_ns));
  LED sA (.in(States_a));
  LED sB (.in(States_b));
  StateVisualisation States (.in_1(register_1_q), .A(States_a), .B(States_b), .C(States_c));
  Register #(.width(2)) register_1 (
    .D(nextstatelogic_1_ns), .en(undriven), .clk(clock_1_out), .Q(register_1_q), .clr(undriven_2));
  // NoConnect on undriven
  // NoConnect on undriven_2
  LED sC (.in(States_c));
  LED alpha (.in(Outputs_alpha));
  LED beta (.in(Outputs_beta));
  OutputVisualisation Outputs (.O(OUTPUT), .alpha(Outputs_alpha), .beta(Outputs_beta), .gamma(Outputs_gamma));
  OutputLogic outputlogic_1 (.S(register_1_q), .O(OUTPUT));
  LED gamma (.in(Outputs_gamma));
endmodule

module NextStateLogic (
  input  [1:0] I,
  input  [1:0] S,
  output [1:0] NS
);

  ROM #(.addrWidth(4), .dataWidth(2)) rom_1 (.addr({S, I}), .data(NS));

  // Notes on the sheet:
  //   contents of rom_1 (hex, n*v repeats v):
  //   0 1 2 0 1 0 2 0 2 1 0 0 4*3
endmodule

module OutputLogic (
  input  [1:0] S,
  output [2:0] O
);

  ROM #(.addrWidth(2), .dataWidth(3)) rom_1 (.addr(S), .data(O));

  // Notes on the sheet:
  //   contents of rom_1 (hex, n*v repeats v):
  //   1 2 4
endmodule

module StateVisualisation (
  input  [1:0] in_1,
  output A,
  output B,
  output C
);

  and and_1 (A, ~in_1[1], ~in_1[0]);  // AND_Gate
  and and_2 (B, ~in_1[1], in_1[0]);  // AND_Gate
  and and_3 (C, in_1[1], ~in_1[0]);  // AND_Gate
endmodule

module InputVisualisation (
  input  [1:0] I,
  output a,
  output b,
  output c,
  output d
);

  and and_1 (a, ~I[1], ~I[0]);  // AND_Gate
  and and_2 (b, I[1], ~I[0]);  // AND_Gate
  and and_3 (c, ~I[1], I[0]);  // AND_Gate
  and and_4 (d, I[1], I[0]);
endmodule

module OutputVisualisation (
  input  [2:0] O,
  output alpha,
  output beta,
  output gamma
);

  and and_1 (alpha, ~O[2], ~O[1], O[0]);  // AND_Gate
  and and_2 (beta, ~O[2], O[1], ~O[0]);  // AND_Gate
  and and_3 (gamma, O[2], ~O[1], ~O[0]);  // AND_Gate
endmodule

module TestSequence (
  input  CLK,
  output [1:0] I_test
);

  wire [3:0] counter_1_q;

  ROM #(.addrWidth(4), .dataWidth(2)) rom_1 (.addr(counter_1_q), .data(I_test));
  Counter #(.max('hf), .width(4)) counter_1 (.Q(counter_1_q), .clk(CLK));  // open: load, D, count, carry, up, clr

  // Notes on the sheet:
  //   contents of rom_1 (hex, n*v repeats v):
  //   0 3 1 0 2 1 1 2 2 1 3 2 0 3 3
endmodule
